// Digital circuit ex3.dig as structural Verilog
module ex3 (
  input  [1:0] A,
  input  [1:0] B,
  output Y
);

  wire and_1_out, and_2_out, and_3_out, B0, B1;

  not not_1 (B1, B[1]);
  not not_2 (B0, B[0]);
  and and_1 (and_1_out, B1, A[1]);
  and and_2 (and_2_out, A[1], A[0], B0);
  and and_3 (and_3_out, A[0], B0, B1);
  or or_1 (Y, and_1_out, and_3_out, and_2_out);
endmodule

/* Test case EX3 Test:
A B Y 

 0b00 0b00 0
 0b00 0b01 0
 0b00 0b10 0
 0b00 0b11 0
 0b01 0b00 1
 0b01 0b01 0
 0b01 0b10 0
 0b01 0b11 0
 0b10 0b00 1
 0b10 0b01 1
 0b10 0b10 0
 0b10 0b11 0
 0b11 0b00 1
 0b11 0b01 1
 0b11 0b10 1
 0b11 0b11 0
*/
